// Digital circuit Flash Memory.dig as structural Verilog
module Flash_Memory (
  input  [15:0] LN,
  input  DAT_dis,
  input  ADR_dis,
  input  CLK,
  output [7:0] Q_CMD,
  output [7:0] Q_DAT,
  output [15:0] Q_ADR
);

  wire d_ff_1_nq, d_ff_2_q, d_ff_3_nq, not_1_out;
  wire [15:0] ADR_d;
  wire [15:8] CMD_d;

  not not_1 (not_1_out, CLK);
  D_FF d_ff_1 (.D(DAT_dis), .C(not_1_out), .nQ(d_ff_1_nq));  // open: Q
  D_FF d_ff_2 (.D(ADR_dis), .C(not_1_out), .Q(d_ff_2_q));  // open: nQ
  D_FF d_ff_3 (.D(d_ff_2_q), .C(not_1_out), .nQ(d_ff_3_nq));  // open: Q
  ROM #(.AddrBits(16), .isProgramMemory("true"), .Bits(16)) CMD (.A(LN), .sel(1'b1), .D({CMD_d, Q_CMD}));
  ROM #(.AddrBits(16), .isProgramMemory("true"), .Bits(16)) ADR (.A(LN), .sel(1'b1), .D(ADR_d));
  assign Q_DAT = d_ff_1_nq ? CMD_d : 8'bz;  // Driver driver_1
  assign Q_ADR = d_ff_3_nq ? ADR_d : 16'bz;  // Driver driver_2

  // Notes on the sheet:
  //   DAT_dis / ADR_dis :
  //   disable the data / address bus
  //   for the next tick in order to
  //   avoid bus collisions
  //   contents of CMD (hex, n*v repeats v):
  //   0,6,0,7,18,1a,8,1a,18,a,18,9,1c,b,18,1a,16,22,18,25,28,1
  //   contents of ADR (hex, n*v repeats v):
  //   0,1,2,1
endmodule
