// Digital circuit RAM.dig as structural Verilog
module RAM (
  input  [7:0] DAT,
  input  [15:0] ADR,
  input  STR,
  input  LD,
  input  CLK,
  output [7:0] Q_DAT
);

  wire d_ff_1_q, not_1_out;

  not not_1 (not_1_out, CLK);
  D_FF d_ff_1 (.D(LD), .C(not_1_out), .Q(d_ff_1_q));  // open: nQ
  RAMDualPort #(.AddrBits(16), .Bits(8)) ramdualport_1 (
    .A(ADR), .Din(DAT), .str(STR), .C(not_1_out), .ld(d_ff_1_q), .D(DAT));

  assign Q_DAT = DAT;

  // Notes on the sheet:
  //   two subsequent load commands can't be performed,
  //   since the previous address stays buffered.
  //   not a problem, just an observation
  //   (since the data after a load command just persists for
  //   one clock pulse, the first operation would be redundant)
  //   str - store to ram
  //   ld - write to data bus
  //    (output enable)
  //   the connection from DAT to Q is 
  //   to mimic the layout of the chip we
  //   are planning on using, as its
  //   i/o is combined into the same pins
endmodule
